// Logisim project MICO.circ as structural Verilog: 13 circuits, main circuit main
module main (
  input  in_1,
  output [31:0] out_2
);

  wire alu_1_zero, clk, mc_1_desvio, mc_1_display, mc_1_fim, mc_1_salto, mc_1_sel_b_const, mc_1_we_rb,
       multiplexer_1_out;
  wire [2:0] mc_1_sel_ula;
  wire [31:0] adder_complete_1_c, alu_1_c, bit_extender_1_out, bit_extender_2_out, im_1_out_2, ip_1_out_5,
       multiplexer_2_out, multiplexer_3_out, rb_1_a, rb_1_b;

  Clock clock_1 (.out(clk));
  Multiplexer multiplexer_1 (.in0(mc_1_salto), .in1(alu_1_zero), .out(multiplexer_1_out), .sel(mc_1_desvio));
  assign bit_extender_1_out = {{16{im_1_out_2[15]}}, im_1_out_2[15:0]};  // Bit_Extender bit_extender_1
  Multiplexer #(.width(32)) multiplexer_2 (
    .in0(32'h1), .in1(bit_extender_1_out), .out(multiplexer_2_out), .sel(multiplexer_1_out));
  adder_complete adder_complete_1 (.A(ip_1_out_5), .B(multiplexer_2_out), .sub(1'b0), .C(adder_complete_1_c));
  IP ip_1 (.instruction(adder_complete_1_c), .fim(mc_1_fim), .clock(clk), .reset(in_1), .out_5(ip_1_out_5));
  IM im_1 (.in_1(ip_1_out_5[23:0]), .out_2(im_1_out_2));
  MC mc_1 (
    .in_1(im_1_out_2[31:28]), .display(mc_1_display), .WE_RB(mc_1_we_rb), .salto(mc_1_salto),
    .desvio(mc_1_desvio), .fim(mc_1_fim), .sel_b_const(mc_1_sel_b_const), .sel_ula(mc_1_sel_ula));
  RB rb_1 (
    .reset(in_1), .clock(clk), .C(alu_1_c), .WE(mc_1_we_rb), .addr_A(im_1_out_2[27:24]),
    .addr_B(im_1_out_2[23:20]), .addr_c(im_1_out_2[19:16]), .A(rb_1_a), .B(rb_1_b));
  assign bit_extender_2_out = {{16{1'b0}}, im_1_out_2[15:0]};  // Bit_Extender bit_extender_2
  Multiplexer #(.width(32)) multiplexer_3 (
    .in0(rb_1_b), .in1(bit_extender_2_out), .out(multiplexer_3_out), .sel(mc_1_sel_b_const));
  ALU alu_1 (.A(rb_1_a), .B(multiplexer_3_out), .sel(mc_1_sel_ula), .zero(alu_1_zero), .C(alu_1_c));
  display display_1 (.A(rb_1_a), .WE(mc_1_display), .clock(clk), .reset(in_1), .display_A(out_2));

  // Other names for the same wires on the sheet: reset = in_1
endmodule

module add (
  input  A,
  input  B,
  input  Cin,
  output Sum,
  output P,
  output G
);

  xor xor_1 (P, A, B);
  xor xor_2 (Sum, P, Cin);
  and and_1 (G, A, B);
endmodule

module four_bit_adder (
  input  B3,
  input  A3,
  input  B2,
  input  A2,
  input  B1,
  input  A1,
  input  B0,
  input  A0,
  input  Cin,
  output S0,
  output S1,
  output S2,
  output S3,
  output C4,
  output GG,
  output PG
);

  wire add_1_g, add_1_p, add_2_g, add_2_p, add_3_g, add_3_p, add_4_g, add_4_p, lookahead_logic_1_c1,
       lookahead_logic_1_c2, lookahead_logic_1_c3;

  add add_1 (.A(A3), .B(B3), .Cin(lookahead_logic_1_c3), .Sum(S3), .P(add_1_p), .G(add_1_g));
  add add_2 (.A(A2), .B(B2), .Cin(lookahead_logic_1_c2), .Sum(S2), .P(add_2_p), .G(add_2_g));
  add add_3 (.A(A1), .B(B1), .Cin(lookahead_logic_1_c1), .Sum(S1), .P(add_3_p), .G(add_3_g));
  lookahead_logic lookahead_logic_1 (
    .C0(Cin), .P0(add_4_p), .G0(add_4_g), .C1(lookahead_logic_1_c1), .P1(add_3_p), .G1(add_3_g),
    .C2(lookahead_logic_1_c2), .P2(add_2_p), .G2(add_2_g), .C3(lookahead_logic_1_c3), .P3(add_1_p),
    .G3(add_1_g), .C4(C4), .PG(PG), .GG(GG));
  add add_4 (.A(A0), .B(B0), .Cin(Cin), .Sum(S0), .P(add_4_p), .G(add_4_g));
endmodule

module lookahead_logic (
  input  C0,
  input  P0,
  input  G0,
  input  P1,
  input  G1,
  input  P2,
  input  G2,
  input  P3,
  input  G3,
  output C1,
  output PG,
  output C2,
  output C3,
  output C4,
  output GG
);

  wire and_1_out, and_2_out, and_3_out, and_4_out, and_5_out, and_6_out, and_7_out, and_8_out, and_9_out,
       and_10_out;

  or or_1 (C1, G0, and_1_out);
  or or_2 (C2, G1, and_2_out, and_3_out);
  or or_3 (C3, G2, and_4_out, and_5_out, and_6_out);
  or or_4 (C4, G3, and_7_out, and_8_out, and_9_out, and_10_out);
  and and_1 (and_1_out, C0, P0);
  and and_2 (and_2_out, C0, P0, P1);
  and and_3 (and_3_out, G0, P1);
  and and_4 (and_4_out, C0, P0, P1, P2);
  and and_5 (and_5_out, G0, P1, P2);
  and and_6 (and_6_out, G1, P2);
  and and_7 (and_7_out, C0, P0, P1, P2, P3);
  and and_8 (and_8_out, G0, P1, P2, P3);
  and and_9 (and_9_out, G1, P2, P3);
  and and_10 (and_10_out, G2, P3);
  and and_11 (PG, P0, P1, P2, P3);
  or or_5 (GG, and_8_out, and_9_out, and_10_out, G3);
endmodule

module adder_complete (
  input  [31:0] A,
  input  [31:0] B,
  input  sub,
  output [31:0] C
);

  wire four_bit_adder_1_gg, four_bit_adder_1_pg, four_bit_adder_2_gg, four_bit_adder_2_pg,
       four_bit_adder_3_gg, four_bit_adder_3_pg, four_bit_adder_4_gg, four_bit_adder_4_pg,
       four_bit_adder_5_gg, four_bit_adder_5_pg, four_bit_adder_6_gg, four_bit_adder_6_pg,
       four_bit_adder_7_gg, four_bit_adder_7_pg, four_bit_adder_8_gg, four_bit_adder_8_pg,
       lookahead_logic_1_c1, lookahead_logic_1_c2, lookahead_logic_1_c3, lookahead_logic_2_c1,
       lookahead_logic_2_c2, lookahead_logic_2_c3, lookahead_logic_2_c4;

  four_bit_adder four_bit_adder_1 (
    .B3(B[31]), .A3(A[31]), .B2(B[30]), .A2(A[30]), .B1(B[29]), .A1(A[29]), .B0(B[28]), .A0(A[28]),
    .GG(four_bit_adder_1_gg), .PG(four_bit_adder_1_pg), .Cin(lookahead_logic_1_c3), .S0(C[28]), .S1(C[29]),
    .S2(C[30]), .S3(C[31]));  // open: C4
  four_bit_adder four_bit_adder_2 (
    .B3(B[27]), .A3(A[27]), .B2(B[26]), .A2(A[26]), .B1(B[25]), .A1(A[25]), .B0(B[24]), .A0(A[24]),
    .GG(four_bit_adder_2_gg), .PG(four_bit_adder_2_pg), .Cin(lookahead_logic_1_c2), .S0(C[24]), .S1(C[25]),
    .S2(C[26]), .S3(C[27]));  // open: C4
  lookahead_logic lookahead_logic_1 (
    .C0(lookahead_logic_2_c4), .P0(four_bit_adder_4_pg), .G0(four_bit_adder_4_gg), .C1(lookahead_logic_1_c1),
    .P1(four_bit_adder_3_pg), .G1(four_bit_adder_3_gg), .C2(lookahead_logic_1_c2), .P2(four_bit_adder_2_pg),
    .G2(four_bit_adder_2_gg), .C3(lookahead_logic_1_c3), .P3(four_bit_adder_1_pg), .G3(four_bit_adder_1_gg));  // open: C4, PG, GG
  four_bit_adder four_bit_adder_3 (
    .B3(B[23]), .A3(A[23]), .B2(B[22]), .A2(A[22]), .B1(B[21]), .A1(A[21]), .B0(B[20]), .A0(A[20]),
    .GG(four_bit_adder_3_gg), .PG(four_bit_adder_3_pg), .Cin(lookahead_logic_1_c1), .S0(C[20]), .S1(C[21]),
    .S2(C[22]), .S3(C[23]));  // open: C4
  four_bit_adder four_bit_adder_4 (
    .B3(B[19]), .A3(A[19]), .B2(B[18]), .A2(A[18]), .B1(B[17]), .A1(A[17]), .B0(B[16]), .A0(A[16]),
    .GG(four_bit_adder_4_gg), .PG(four_bit_adder_4_pg), .Cin(lookahead_logic_2_c4), .S0(C[16]), .S1(C[17]),
    .S2(C[18]), .S3(C[19]));  // open: C4
  four_bit_adder four_bit_adder_5 (
    .B3(B[15]), .A3(A[15]), .B2(B[14]), .A2(A[14]), .B1(B[13]), .A1(A[13]), .B0(B[12]), .A0(A[12]),
    .GG(four_bit_adder_5_gg), .PG(four_bit_adder_5_pg), .Cin(lookahead_logic_2_c3), .S0(C[12]), .S1(C[13]),
    .S2(C[14]), .S3(C[15]));  // open: C4
  four_bit_adder four_bit_adder_6 (
    .B3(B[11]), .A3(A[11]), .B2(B[10]), .A2(A[10]), .B1(B[9]), .A1(A[9]), .B0(B[8]), .A0(A[8]),
    .GG(four_bit_adder_6_gg), .PG(four_bit_adder_6_pg), .Cin(lookahead_logic_2_c2), .S0(C[8]), .S1(C[9]),
    .S2(C[10]), .S3(C[11]));  // open: C4
  lookahead_logic lookahead_logic_2 (
    .C0(sub), .P0(four_bit_adder_8_pg), .G0(four_bit_adder_8_gg), .C1(lookahead_logic_2_c1),
    .P1(four_bit_adder_7_pg), .G1(four_bit_adder_7_gg), .C2(lookahead_logic_2_c2), .P2(four_bit_adder_6_pg),
    .G2(four_bit_adder_6_gg), .C3(lookahead_logic_2_c3), .P3(four_bit_adder_5_pg), .G3(four_bit_adder_5_gg),
    .C4(lookahead_logic_2_c4));  // open: PG, GG
  four_bit_adder four_bit_adder_7 (
    .B3(B[7]), .A3(A[7]), .B2(B[6]), .A2(A[6]), .B1(B[5]), .A1(A[5]), .B0(B[4]), .A0(A[4]),
    .GG(four_bit_adder_7_gg), .PG(four_bit_adder_7_pg), .Cin(lookahead_logic_2_c1), .S0(C[4]), .S1(C[5]),
    .S2(C[6]), .S3(C[7]));  // open: C4
  four_bit_adder four_bit_adder_8 (
    .B3(B[3]), .A3(A[3]), .B2(B[2]), .A2(A[2]), .B1(B[1]), .A1(A[1]), .B0(B[0]), .A0(A[0]),
    .GG(four_bit_adder_8_gg), .PG(four_bit_adder_8_pg), .Cin(sub), .S0(C[0]), .S1(C[1]), .S2(C[2]), .S3(C[3]));  // open: C4
endmodule

module RB (
  input  reset,
  input  clock,
  input  [31:0] C,
  input  WE,
  input  [3:0] addr_A,
  input  [3:0] addr_B,
  input  [3:0] addr_c,
  output [31:0] A,
  output [31:0] B
);

  wire WE_addr_1, WE_addr_2, WE_addr_3, WE_addr_4, WE_addr_5, WE_addr_6, WE_addr_7, WE_addr_8, WE_addr_9,
       WE_addr_10, WE_addr_11, WE_addr_12, WE_addr_13, WE_addr_14, WE_addr_15;
  wire [31:0] addr_0, addr_1, addr_2, addr_3, addr_4, addr_5, addr_6, addr_7, addr_8, addr_9, addr_10,
       addr_11, addr_12, addr_13, addr_14, addr_15;

  Demultiplexer #(.select(4)) demultiplexer_1 (
    .out1(WE_addr_1), .out2(WE_addr_2), .out3(WE_addr_3), .out4(WE_addr_4), .out5(WE_addr_5),
    .out6(WE_addr_6), .out7(WE_addr_7), .out8(WE_addr_8), .out9(WE_addr_9), .out10(WE_addr_10),
    .out11(WE_addr_11), .out12(WE_addr_12), .out13(WE_addr_13), .out14(WE_addr_14), .out15(WE_addr_15),
    .in(WE), .sel(addr_c));  // open: out0
  Register #(.width(32)) register_1 (.D(C), .en(1'b0), .clk(clock), .Q(addr_0), .clr(reset));
  Register #(.width(32)) register_2 (.D(C), .en(WE_addr_1), .clk(clock), .Q(addr_1), .clr(reset));
  Register #(.width(32)) register_3 (.D(C), .en(WE_addr_2), .clk(clock), .Q(addr_2), .clr(reset));
  Register #(.width(32)) register_4 (.D(C), .en(WE_addr_3), .clk(clock), .Q(addr_3), .clr(reset));
  Register #(.width(32)) register_5 (.D(C), .en(WE_addr_4), .clk(clock), .Q(addr_4), .clr(reset));
  Register #(.width(32)) register_6 (.D(C), .en(WE_addr_5), .clk(clock), .Q(addr_5), .clr(reset));
  Register #(.width(32)) register_7 (.D(C), .en(WE_addr_6), .clk(clock), .Q(addr_6), .clr(reset));
  Register #(.width(32)) register_8 (.D(C), .en(WE_addr_7), .clk(clock), .Q(addr_7), .clr(reset));
  Register #(.width(32)) register_9 (.D(C), .en(WE_addr_8), .clk(clock), .Q(addr_8), .clr(reset));
  Register #(.width(32)) register_10 (.D(C), .en(WE_addr_9), .clk(clock), .Q(addr_9), .clr(reset));
  Register #(.width(32)) register_11 (.D(C), .en(WE_addr_10), .clk(clock), .Q(addr_10), .clr(reset));
  Register #(.width(32)) register_12 (.D(C), .en(WE_addr_11), .clk(clock), .Q(addr_11), .clr(reset));
  Register #(.width(32)) register_13 (.D(C), .en(WE_addr_12), .clk(clock), .Q(addr_12), .clr(reset));
  Register #(.width(32)) register_14 (.D(C), .en(WE_addr_13), .clk(clock), .Q(addr_13), .clr(reset));
  Register #(.width(32)) register_15 (.D(C), .en(WE_addr_14), .clk(clock), .Q(addr_14), .clr(reset));
  Register #(.width(32)) register_16 (.D(C), .en(WE_addr_15), .clk(clock), .Q(addr_15), .clr(reset));
  Multiplexer #(.select(4), .width(32)) multiplexer_1 (
    .in0(addr_0), .in1(addr_1), .in2(addr_2), .in3(addr_3), .in4(addr_4), .in5(addr_5), .in6(addr_6),
    .in7(addr_7), .in8(addr_8), .in9(addr_9), .in10(addr_10), .in11(addr_11), .in12(addr_12), .in13(addr_13),
    .in14(addr_14), .in15(addr_15), .out(A), .sel(addr_A));
  Multiplexer #(.select(4), .width(32)) multiplexer_2 (
    .in0(addr_0), .in1(addr_1), .in2(addr_2), .in3(addr_3), .in4(addr_4), .in5(addr_5), .in6(addr_6),
    .in7(addr_7), .in8(addr_8), .in9(addr_9), .in10(addr_10), .in11(addr_11), .in12(addr_12), .in13(addr_13),
    .in14(addr_14), .in15(addr_15), .out(B), .sel(addr_B));
endmodule

module add_sub (
  input  [31:0] A,
  input  [31:0] B,
  input  sub,
  output [31:0] C
);

  wire [31:0] multiplexer_1_out, not_1_out;

  assign not_1_out = ~B;  // NOT_Gate not_1, 32 bits wide
  Multiplexer #(.width(32)) multiplexer_1 (.in0(B), .in1(not_1_out), .out(multiplexer_1_out), .sel(sub));
  adder_complete adder_complete_1 (.A(A), .B(multiplexer_1_out), .sub(sub), .C(C));
endmodule

module bit_shifter_test (
  input  [31:0] A,
  input  L,
  input  R,
  input  [4:0] B,
  output [31:0] C
);

  wire multiplexer_1_out, multiplexer_2_out, multiplexer_3_out, multiplexer_4_out, multiplexer_5_out,
       multiplexer_6_out, multiplexer_7_out, multiplexer_8_out, multiplexer_9_out, multiplexer_10_out,
       multiplexer_11_out, multiplexer_12_out, multiplexer_13_out, multiplexer_14_out, multiplexer_15_out,
       multiplexer_16_out, multiplexer_17_out, multiplexer_18_out, multiplexer_19_out, multiplexer_20_out,
       multiplexer_21_out, multiplexer_22_out, multiplexer_23_out, multiplexer_24_out, multiplexer_25_out,
       multiplexer_26_out, multiplexer_27_out, multiplexer_28_out, multiplexer_29_out, multiplexer_30_out,
       multiplexer_31_out, multiplexer_32_out, multiplexer_33_out, multiplexer_34_out, multiplexer_35_out,
       multiplexer_36_out, multiplexer_37_out, multiplexer_38_out, multiplexer_39_out, multiplexer_40_out,
       multiplexer_41_out, multiplexer_42_out, multiplexer_43_out, multiplexer_44_out, multiplexer_45_out,
       multiplexer_46_out, multiplexer_47_out, multiplexer_48_out, multiplexer_49_out, multiplexer_50_out,
       multiplexer_51_out, multiplexer_52_out, multiplexer_53_out, multiplexer_54_out, multiplexer_55_out,
       multiplexer_56_out, multiplexer_57_out, multiplexer_58_out, multiplexer_59_out, multiplexer_60_out,
       multiplexer_61_out, multiplexer_62_out, multiplexer_63_out, multiplexer_64_out, multiplexer_65_out,
       multiplexer_66_out, multiplexer_67_out, multiplexer_68_out, multiplexer_69_out, multiplexer_70_out,
       multiplexer_71_out, multiplexer_72_out, multiplexer_73_out, multiplexer_74_out, multiplexer_75_out,
       multiplexer_76_out, multiplexer_77_out, multiplexer_78_out, multiplexer_79_out, multiplexer_80_out,
       multiplexer_81_out, multiplexer_82_out, multiplexer_83_out, multiplexer_84_out, multiplexer_85_out,
       multiplexer_86_out, multiplexer_87_out, multiplexer_88_out, multiplexer_89_out, multiplexer_90_out,
       multiplexer_91_out, multiplexer_92_out, multiplexer_93_out, multiplexer_94_out, multiplexer_95_out,
       multiplexer_96_out, multiplexer_97_out, multiplexer_98_out, multiplexer_99_out, multiplexer_100_out,
       multiplexer_101_out, multiplexer_102_out, multiplexer_103_out, multiplexer_104_out,
       multiplexer_105_out, multiplexer_106_out, multiplexer_107_out, multiplexer_108_out,
       multiplexer_109_out, multiplexer_110_out, multiplexer_111_out, multiplexer_112_out,
       multiplexer_113_out, multiplexer_114_out, multiplexer_115_out, multiplexer_116_out,
       multiplexer_117_out, multiplexer_118_out, multiplexer_119_out, multiplexer_120_out,
       multiplexer_121_out, multiplexer_122_out, multiplexer_123_out, multiplexer_124_out,
       multiplexer_125_out, multiplexer_126_out, multiplexer_127_out, multiplexer_128_out, not_1_out,
       not_2_out, not_3_out, not_4_out, not_5_out;
  wire [1:0] selector_1, selector_2, selector_3, selector_4, selector_5;

  Multiplexer #(.select(2)) multiplexer_1 (
    .in0(A[0]), .in1(1'b0), .in2(A[1]), .in3(A[0]), .out(multiplexer_1_out), .sel(selector_1));
  Multiplexer #(.select(2)) multiplexer_2 (
    .in0(A[1]), .in1(A[0]), .in2(A[2]), .in3(A[1]), .out(multiplexer_2_out), .sel(selector_1));
  Multiplexer #(.select(2)) multiplexer_3 (
    .in0(A[2]), .in1(A[1]), .in2(A[3]), .in3(A[2]), .out(multiplexer_3_out), .sel(selector_1));
  Multiplexer #(.select(2)) multiplexer_4 (
    .in0(A[3]), .in1(A[2]), .in2(A[4]), .in3(A[3]), .out(multiplexer_4_out), .sel(selector_1));
  Multiplexer #(.select(2)) multiplexer_5 (
    .in0(A[4]), .in1(A[3]), .in2(A[5]), .in3(A[4]), .out(multiplexer_5_out), .sel(selector_1));
  Multiplexer #(.select(2)) multiplexer_6 (
    .in0(A[5]), .in1(A[4]), .in2(A[6]), .in3(A[5]), .out(multiplexer_6_out), .sel(selector_1));
  Multiplexer #(.select(2)) multiplexer_7 (
    .in0(A[6]), .in1(A[5]), .in2(A[7]), .in3(A[6]), .out(multiplexer_7_out), .sel(selector_1));
  Multiplexer #(.select(2)) multiplexer_8 (
    .in0(A[7]), .in1(A[6]), .in2(A[8]), .in3(A[7]), .out(multiplexer_8_out), .sel(selector_1));
  Multiplexer #(.select(2)) multiplexer_9 (
    .in0(A[8]), .in1(A[7]), .in2(A[9]), .in3(A[8]), .out(multiplexer_9_out), .sel(selector_1));
  Multiplexer #(.select(2)) multiplexer_10 (
    .in0(A[9]), .in1(A[8]), .in2(A[10]), .in3(A[9]), .out(multiplexer_10_out), .sel(selector_1));
  Multiplexer #(.select(2)) multiplexer_11 (
    .in0(A[10]), .in1(A[9]), .in2(A[11]), .in3(A[10]), .out(multiplexer_11_out), .sel(selector_1));
  Multiplexer #(.select(2)) multiplexer_12 (
    .in0(A[11]), .in1(A[10]), .in2(A[12]), .in3(A[11]), .out(multiplexer_12_out), .sel(selector_1));
  Multiplexer #(.select(2)) multiplexer_13 (
    .in0(A[12]), .in1(A[11]), .in2(A[13]), .in3(A[12]), .out(multiplexer_13_out), .sel(selector_1));
  Multiplexer #(.select(2)) multiplexer_14 (
    .in0(A[13]), .in1(A[12]), .in2(A[14]), .in3(A[13]), .out(multiplexer_14_out), .sel(selector_1));
  Multiplexer #(.select(2)) multiplexer_15 (
    .in0(A[14]), .in1(A[13]), .in2(A[15]), .in3(A[14]), .out(multiplexer_15_out), .sel(selector_1));
  Multiplexer #(.select(2)) multiplexer_16 (
    .in0(A[15]), .in1(A[14]), .in2(A[16]), .in3(A[15]), .out(multiplexer_16_out), .sel(selector_1));
  Multiplexer #(.select(2)) multiplexer_17 (
    .in0(A[16]), .in1(A[15]), .in2(A[17]), .in3(A[16]), .out(multiplexer_17_out), .sel(selector_1));
  Multiplexer #(.select(2)) multiplexer_18 (
    .in0(A[17]), .in1(A[16]), .in2(A[18]), .in3(A[17]), .out(multiplexer_18_out), .sel(selector_1));
  Multiplexer #(.select(2)) multiplexer_19 (
    .in0(A[18]), .in1(A[17]), .in2(A[19]), .in3(A[18]), .out(multiplexer_19_out), .sel(selector_1));
  Multiplexer #(.select(2)) multiplexer_20 (
    .in0(A[19]), .in1(A[18]), .in2(A[20]), .in3(A[19]), .out(multiplexer_20_out), .sel(selector_1));
  Multiplexer #(.select(2)) multiplexer_21 (
    .in0(A[20]), .in1(A[19]), .in2(A[21]), .in3(A[20]), .out(multiplexer_21_out), .sel(selector_1));
  Multiplexer #(.select(2)) multiplexer_22 (
    .in0(A[21]), .in1(A[20]), .in2(A[22]), .in3(A[21]), .out(multiplexer_22_out), .sel(selector_1));
  Multiplexer #(.select(2)) multiplexer_23 (
    .in0(A[22]), .in1(A[21]), .in2(A[23]), .in3(A[22]), .out(multiplexer_23_out), .sel(selector_1));
  Multiplexer #(.select(2)) multiplexer_24 (
    .in0(A[23]), .in1(A[22]), .in2(A[24]), .in3(A[23]), .out(multiplexer_24_out), .sel(selector_1));
  Multiplexer #(.select(2)) multiplexer_25 (
    .in0(A[24]), .in1(A[23]), .in2(A[25]), .in3(A[24]), .out(multiplexer_25_out), .sel(selector_1));
  Multiplexer #(.select(2)) multiplexer_26 (
    .in0(A[25]), .in1(A[24]), .in2(A[26]), .in3(A[25]), .out(multiplexer_26_out), .sel(selector_1));
  Multiplexer #(.select(2)) multiplexer_27 (
    .in0(A[26]), .in1(A[25]), .in2(A[27]), .in3(A[26]), .out(multiplexer_27_out), .sel(selector_1));
  Multiplexer #(.select(2)) multiplexer_28 (
    .in0(A[27]), .in1(A[26]), .in2(A[28]), .in3(A[27]), .out(multiplexer_28_out), .sel(selector_1));
  Multiplexer #(.select(2)) multiplexer_29 (
    .in0(A[28]), .in1(A[27]), .in2(A[29]), .in3(A[28]), .out(multiplexer_29_out), .sel(selector_1));
  Multiplexer #(.select(2)) multiplexer_30 (
    .in0(A[29]), .in1(A[28]), .in2(A[30]), .in3(A[29]), .out(multiplexer_30_out), .sel(selector_1));
  Multiplexer #(.select(2)) multiplexer_31 (
    .in0(A[30]), .in1(A[29]), .in2(A[31]), .in3(A[30]), .out(multiplexer_31_out), .sel(selector_1));
  Multiplexer #(.select(2)) multiplexer_32 (
    .in0(A[31]), .in1(A[30]), .in2(1'b0), .in3(A[31]), .out(multiplexer_32_out), .sel(selector_1));
  BitSelector #(.group(2), .width(2)) bitselector_1 (.in({R, L}), .out(selector_5), .sel(not_1_out));
  not not_1 (not_1_out, B[4]);
  Multiplexer #(.select(2)) multiplexer_33 (
    .in0(multiplexer_1_out), .in1(1'b0), .in2(multiplexer_3_out), .in3(multiplexer_1_out),
    .out(multiplexer_33_out), .sel(selector_2));
  Multiplexer #(.select(2)) multiplexer_34 (
    .in0(multiplexer_2_out), .in1(1'b0), .in2(multiplexer_4_out), .in3(multiplexer_2_out),
    .out(multiplexer_34_out), .sel(selector_2));
  Multiplexer #(.select(2)) multiplexer_35 (
    .in0(multiplexer_3_out), .in1(multiplexer_1_out), .in2(multiplexer_5_out), .in3(multiplexer_3_out),
    .out(multiplexer_35_out), .sel(selector_2));
  Multiplexer #(.select(2)) multiplexer_36 (
    .in0(multiplexer_4_out), .in1(multiplexer_2_out), .in2(multiplexer_6_out), .in3(multiplexer_4_out),
    .out(multiplexer_36_out), .sel(selector_2));
  Multiplexer #(.select(2)) multiplexer_37 (
    .in0(multiplexer_5_out), .in1(multiplexer_3_out), .in2(multiplexer_7_out), .in3(multiplexer_5_out),
    .out(multiplexer_37_out), .sel(selector_2));
  Multiplexer #(.select(2)) multiplexer_38 (
    .in0(multiplexer_6_out), .in1(multiplexer_4_out), .in2(multiplexer_8_out), .in3(multiplexer_6_out),
    .out(multiplexer_38_out), .sel(selector_2));
  Multiplexer #(.select(2)) multiplexer_39 (
    .in0(multiplexer_7_out), .in1(multiplexer_5_out), .in2(multiplexer_9_out), .in3(multiplexer_7_out),
    .out(multiplexer_39_out), .sel(selector_2));
  Multiplexer #(.select(2)) multiplexer_40 (
    .in0(multiplexer_8_out), .in1(multiplexer_6_out), .in2(multiplexer_10_out), .in3(multiplexer_8_out),
    .out(multiplexer_40_out), .sel(selector_2));
  Multiplexer #(.select(2)) multiplexer_41 (
    .in0(multiplexer_9_out), .in1(multiplexer_7_out), .in2(multiplexer_11_out), .in3(multiplexer_9_out),
    .out(multiplexer_41_out), .sel(selector_2));
  Multiplexer #(.select(2)) multiplexer_42 (
    .in0(multiplexer_10_out), .in1(multiplexer_8_out), .in2(multiplexer_12_out), .in3(multiplexer_10_out),
    .out(multiplexer_42_out), .sel(selector_2));
  Multiplexer #(.select(2)) multiplexer_43 (
    .in0(multiplexer_11_out), .in1(multiplexer_9_out), .in2(multiplexer_13_out), .in3(multiplexer_11_out),
    .out(multiplexer_43_out), .sel(selector_2));
  Multiplexer #(.select(2)) multiplexer_44 (
    .in0(multiplexer_12_out), .in1(multiplexer_10_out), .in2(multiplexer_14_out), .in3(multiplexer_12_out),
    .out(multiplexer_44_out), .sel(selector_2));
  Multiplexer #(.select(2)) multiplexer_45 (
    .in0(multiplexer_13_out), .in1(multiplexer_11_out), .in2(multiplexer_15_out), .in3(multiplexer_13_out),
    .out(multiplexer_45_out), .sel(selector_2));
  Multiplexer #(.select(2)) multiplexer_46 (
    .in0(multiplexer_14_out), .in1(multiplexer_12_out), .in2(multiplexer_16_out), .in3(multiplexer_14_out),
    .out(multiplexer_46_out), .sel(selector_2));
  Multiplexer #(.select(2)) multiplexer_47 (
    .in0(multiplexer_15_out), .in1(multiplexer_13_out), .in2(multiplexer_17_out), .in3(multiplexer_15_out),
    .out(multiplexer_47_out), .sel(selector_2));
  Multiplexer #(.select(2)) multiplexer_48 (
    .in0(multiplexer_16_out), .in1(multiplexer_14_out), .in2(multiplexer_18_out), .in3(multiplexer_16_out),
    .out(multiplexer_48_out), .sel(selector_2));
  Multiplexer #(.select(2)) multiplexer_49 (
    .in0(multiplexer_17_out), .in1(multiplexer_15_out), .in2(multiplexer_19_out), .in3(multiplexer_17_out),
    .out(multiplexer_49_out), .sel(selector_2));
  Multiplexer #(.select(2)) multiplexer_50 (
    .in0(multiplexer_18_out), .in1(multiplexer_16_out), .in2(multiplexer_20_out), .in3(multiplexer_18_out),
    .out(multiplexer_50_out), .sel(selector_2));
  Multiplexer #(.select(2)) multiplexer_51 (
    .in0(multiplexer_19_out), .in1(multiplexer_17_out), .in2(multiplexer_21_out), .in3(multiplexer_19_out),
    .out(multiplexer_51_out), .sel(selector_2));
  Multiplexer #(.select(2)) multiplexer_52 (
    .in0(multiplexer_20_out), .in1(multiplexer_18_out), .in2(multiplexer_22_out), .in3(multiplexer_20_out),
    .out(multiplexer_52_out), .sel(selector_2));
  Multiplexer #(.select(2)) multiplexer_53 (
    .in0(multiplexer_21_out), .in1(multiplexer_19_out), .in2(multiplexer_23_out), .in3(multiplexer_21_out),
    .out(multiplexer_53_out), .sel(selector_2));
  Multiplexer #(.select(2)) multiplexer_54 (
    .in0(multiplexer_22_out), .in1(multiplexer_20_out), .in2(multiplexer_24_out), .in3(multiplexer_22_out),
    .out(multiplexer_54_out), .sel(selector_2));
  Multiplexer #(.select(2)) multiplexer_55 (
    .in0(multiplexer_23_out), .in1(multiplexer_21_out), .in2(multiplexer_25_out), .in3(multiplexer_23_out),
    .out(multiplexer_55_out), .sel(selector_2));
  Multiplexer #(.select(2)) multiplexer_56 (
    .in0(multiplexer_24_out), .in1(multiplexer_22_out), .in2(multiplexer_26_out), .in3(multiplexer_24_out),
    .out(multiplexer_56_out), .sel(selector_2));
  Multiplexer #(.select(2)) multiplexer_57 (
    .in0(multiplexer_25_out), .in1(multiplexer_23_out), .in2(multiplexer_27_out), .in3(multiplexer_25_out),
    .out(multiplexer_57_out), .sel(selector_2));
  Multiplexer #(.select(2)) multiplexer_58 (
    .in0(multiplexer_26_out), .in1(multiplexer_24_out), .in2(multiplexer_28_out), .in3(multiplexer_26_out),
    .out(multiplexer_58_out), .sel(selector_2));
  Multiplexer #(.select(2)) multiplexer_59 (
    .in0(multiplexer_27_out), .in1(multiplexer_25_out), .in2(multiplexer_29_out), .in3(multiplexer_27_out),
    .out(multiplexer_59_out), .sel(selector_2));
  Multiplexer #(.select(2)) multiplexer_60 (
    .in0(multiplexer_28_out), .in1(multiplexer_26_out), .in2(multiplexer_30_out), .in3(multiplexer_28_out),
    .out(multiplexer_60_out), .sel(selector_2));
  Multiplexer #(.select(2)) multiplexer_61 (
    .in0(multiplexer_29_out), .in1(multiplexer_27_out), .in2(multiplexer_31_out), .in3(multiplexer_29_out),
    .out(multiplexer_61_out), .sel(selector_2));
  Multiplexer #(.select(2)) multiplexer_62 (
    .in0(multiplexer_30_out), .in1(multiplexer_28_out), .in2(multiplexer_32_out), .in3(multiplexer_30_out),
    .out(multiplexer_62_out), .sel(selector_2));
  Multiplexer #(.select(2)) multiplexer_63 (
    .in0(multiplexer_31_out), .in1(multiplexer_29_out), .in2(1'b0), .in3(multiplexer_31_out),
    .out(multiplexer_63_out), .sel(selector_2));
  Multiplexer #(.select(2)) multiplexer_64 (
    .in0(multiplexer_32_out), .in1(multiplexer_30_out), .in2(1'b0), .in3(multiplexer_32_out),
    .out(multiplexer_64_out), .sel(selector_2));
  BitSelector #(.group(2), .width(2)) bitselector_2 (.in({R, L}), .out(selector_4), .sel(not_2_out));
  not not_2 (not_2_out, B[3]);
  not not_3 (not_3_out, B[2]);
  Multiplexer #(.select(2)) multiplexer_65 (
    .in0(multiplexer_33_out), .in1(1'b0), .in2(multiplexer_37_out), .in3(multiplexer_33_out),
    .out(multiplexer_65_out), .sel(selector_3));
  Multiplexer #(.select(2)) multiplexer_66 (
    .in0(multiplexer_34_out), .in1(1'b0), .in2(multiplexer_38_out), .in3(multiplexer_34_out),
    .out(multiplexer_66_out), .sel(selector_3));
  Multiplexer #(.select(2)) multiplexer_67 (
    .in0(multiplexer_35_out), .in1(1'b0), .in2(multiplexer_39_out), .in3(multiplexer_35_out),
    .out(multiplexer_67_out), .sel(selector_3));
  Multiplexer #(.select(2)) multiplexer_68 (
    .in0(multiplexer_36_out), .in1(1'b0), .in2(multiplexer_40_out), .in3(multiplexer_36_out),
    .out(multiplexer_68_out), .sel(selector_3));
  Multiplexer #(.select(2)) multiplexer_69 (
    .in0(multiplexer_37_out), .in1(multiplexer_33_out), .in2(multiplexer_41_out), .in3(multiplexer_37_out),
    .out(multiplexer_69_out), .sel(selector_3));
  Multiplexer #(.select(2)) multiplexer_70 (
    .in0(multiplexer_38_out), .in1(multiplexer_34_out), .in2(multiplexer_42_out), .in3(multiplexer_38_out),
    .out(multiplexer_70_out), .sel(selector_3));
  Multiplexer #(.select(2)) multiplexer_71 (
    .in0(multiplexer_39_out), .in1(multiplexer_35_out), .in2(multiplexer_43_out), .in3(multiplexer_39_out),
    .out(multiplexer_71_out), .sel(selector_3));
  Multiplexer #(.select(2)) multiplexer_72 (
    .in0(multiplexer_40_out), .in1(multiplexer_36_out), .in2(multiplexer_44_out), .in3(multiplexer_40_out),
    .out(multiplexer_72_out), .sel(selector_3));
  Multiplexer #(.select(2)) multiplexer_73 (
    .in0(multiplexer_41_out), .in1(multiplexer_37_out), .in2(multiplexer_45_out), .in3(multiplexer_41_out),
    .out(multiplexer_73_out), .sel(selector_3));
  Multiplexer #(.select(2)) multiplexer_74 (
    .in0(multiplexer_42_out), .in1(multiplexer_38_out), .in2(multiplexer_46_out), .in3(multiplexer_42_out),
    .out(multiplexer_74_out), .sel(selector_3));
  Multiplexer #(.select(2)) multiplexer_75 (
    .in0(multiplexer_43_out), .in1(multiplexer_39_out), .in2(multiplexer_47_out), .in3(multiplexer_43_out),
    .out(multiplexer_75_out), .sel(selector_3));
  Multiplexer #(.select(2)) multiplexer_76 (
    .in0(multiplexer_44_out), .in1(multiplexer_40_out), .in2(multiplexer_48_out), .in3(multiplexer_44_out),
    .out(multiplexer_76_out), .sel(selector_3));
  Multiplexer #(.select(2)) multiplexer_77 (
    .in0(multiplexer_45_out), .in1(multiplexer_41_out), .in2(multiplexer_49_out), .in3(multiplexer_45_out),
    .out(multiplexer_77_out), .sel(selector_3));
  Multiplexer #(.select(2)) multiplexer_78 (
    .in0(multiplexer_46_out), .in1(multiplexer_42_out), .in2(multiplexer_50_out), .in3(multiplexer_46_out),
    .out(multiplexer_78_out), .sel(selector_3));
  Multiplexer #(.select(2)) multiplexer_79 (
    .in0(multiplexer_47_out), .in1(multiplexer_43_out), .in2(multiplexer_51_out), .in3(multiplexer_47_out),
    .out(multiplexer_79_out), .sel(selector_3));
  Multiplexer #(.select(2)) multiplexer_80 (
    .in0(multiplexer_48_out), .in1(multiplexer_44_out), .in2(multiplexer_52_out), .in3(multiplexer_48_out),
    .out(multiplexer_80_out), .sel(selector_3));
  Multiplexer #(.select(2)) multiplexer_81 (
    .in0(multiplexer_49_out), .in1(multiplexer_45_out), .in2(multiplexer_53_out), .in3(multiplexer_49_out),
    .out(multiplexer_81_out), .sel(selector_3));
  Multiplexer #(.select(2)) multiplexer_82 (
    .in0(multiplexer_50_out), .in1(multiplexer_46_out), .in2(multiplexer_54_out), .in3(multiplexer_50_out),
    .out(multiplexer_82_out), .sel(selector_3));
  Multiplexer #(.select(2)) multiplexer_83 (
    .in0(multiplexer_51_out), .in1(multiplexer_47_out), .in2(multiplexer_55_out), .in3(multiplexer_51_out),
    .out(multiplexer_83_out), .sel(selector_3));
  Multiplexer #(.select(2)) multiplexer_84 (
    .in0(multiplexer_52_out), .in1(multiplexer_48_out), .in2(multiplexer_56_out), .in3(multiplexer_52_out),
    .out(multiplexer_84_out), .sel(selector_3));
  Multiplexer #(.select(2)) multiplexer_85 (
    .in0(multiplexer_53_out), .in1(multiplexer_49_out), .in2(multiplexer_57_out), .in3(multiplexer_53_out),
    .out(multiplexer_85_out), .sel(selector_3));
  Multiplexer #(.select(2)) multiplexer_86 (
    .in0(multiplexer_54_out), .in1(multiplexer_50_out), .in2(multiplexer_58_out), .in3(multiplexer_54_out),
    .out(multiplexer_86_out), .sel(selector_3));
  Multiplexer #(.select(2)) multiplexer_87 (
    .in0(multiplexer_55_out), .in1(multiplexer_51_out), .in2(multiplexer_59_out), .in3(multiplexer_55_out),
    .out(multiplexer_87_out), .sel(selector_3));
  Multiplexer #(.select(2)) multiplexer_88 (
    .in0(multiplexer_56_out), .in1(multiplexer_52_out), .in2(multiplexer_60_out), .in3(multiplexer_56_out),
    .out(multiplexer_88_out), .sel(selector_3));
  Multiplexer #(.select(2)) multiplexer_89 (
    .in0(multiplexer_57_out), .in1(multiplexer_53_out), .in2(multiplexer_61_out), .in3(multiplexer_57_out),
    .out(multiplexer_89_out), .sel(selector_3));
  Multiplexer #(.select(2)) multiplexer_90 (
    .in0(multiplexer_58_out), .in1(multiplexer_54_out), .in2(multiplexer_62_out), .in3(multiplexer_58_out),
    .out(multiplexer_90_out), .sel(selector_3));
  Multiplexer #(.select(2)) multiplexer_91 (
    .in0(multiplexer_59_out), .in1(multiplexer_55_out), .in2(multiplexer_63_out), .in3(multiplexer_59_out),
    .out(multiplexer_91_out), .sel(selector_3));
  Multiplexer #(.select(2)) multiplexer_92 (
    .in0(multiplexer_60_out), .in1(multiplexer_56_out), .in2(multiplexer_64_out), .in3(multiplexer_60_out),
    .out(multiplexer_92_out), .sel(selector_3));
  Multiplexer #(.select(2)) multiplexer_93 (
    .in0(multiplexer_61_out), .in1(multiplexer_57_out), .in2(1'b0), .in3(multiplexer_61_out),
    .out(multiplexer_93_out), .sel(selector_3));
  Multiplexer #(.select(2)) multiplexer_94 (
    .in0(multiplexer_62_out), .in1(multiplexer_58_out), .in2(1'b0), .in3(multiplexer_62_out),
    .out(multiplexer_94_out), .sel(selector_3));
  Multiplexer #(.select(2)) multiplexer_95 (
    .in0(multiplexer_63_out), .in1(multiplexer_59_out), .in2(1'b0), .in3(multiplexer_63_out),
    .out(multiplexer_95_out), .sel(selector_3));
  Multiplexer #(.select(2)) multiplexer_96 (
    .in0(multiplexer_64_out), .in1(multiplexer_60_out), .in2(1'b0), .in3(multiplexer_64_out),
    .out(multiplexer_96_out), .sel(selector_3));
  BitSelector #(.group(2), .width(2)) bitselector_3 (.in({R, L}), .out(selector_3), .sel(not_3_out));
  BitSelector #(.group(2), .width(2)) bitselector_4 (.in({R, L}), .out(selector_2), .sel(not_4_out));
  not not_4 (not_4_out, B[1]);
  BitSelector #(.group(2), .width(2)) bitselector_5 (.in({R, L}), .out(selector_1), .sel(not_5_out));
  not not_5 (not_5_out, B[0]);
  Multiplexer #(.select(2)) multiplexer_97 (
    .in0(multiplexer_65_out), .in1(1'b0), .in2(multiplexer_73_out), .in3(multiplexer_65_out),
    .out(multiplexer_97_out), .sel(selector_4));
  Multiplexer #(.select(2)) multiplexer_98 (
    .in0(multiplexer_66_out), .in1(1'b0), .in2(multiplexer_74_out), .in3(multiplexer_66_out),
    .out(multiplexer_98_out), .sel(selector_4));
  Multiplexer #(.select(2)) multiplexer_99 (
    .in0(multiplexer_67_out), .in1(1'b0), .in2(multiplexer_75_out), .in3(multiplexer_67_out),
    .out(multiplexer_99_out), .sel(selector_4));
  Multiplexer #(.select(2)) multiplexer_100 (
    .in0(multiplexer_68_out), .in1(1'b0), .in2(multiplexer_76_out), .in3(multiplexer_68_out),
    .out(multiplexer_100_out), .sel(selector_4));
  Multiplexer #(.select(2)) multiplexer_101 (
    .in0(multiplexer_69_out), .in1(1'b0), .in2(multiplexer_77_out), .in3(multiplexer_69_out),
    .out(multiplexer_101_out), .sel(selector_4));
  Multiplexer #(.select(2)) multiplexer_102 (
    .in0(multiplexer_70_out), .in1(1'b0), .in2(multiplexer_78_out), .in3(multiplexer_70_out),
    .out(multiplexer_102_out), .sel(selector_4));
  Multiplexer #(.select(2)) multiplexer_103 (
    .in0(multiplexer_71_out), .in1(1'b0), .in2(multiplexer_79_out), .in3(multiplexer_71_out),
    .out(multiplexer_103_out), .sel(selector_4));
  Multiplexer #(.select(2)) multiplexer_104 (
    .in0(multiplexer_72_out), .in1(1'b0), .in2(multiplexer_80_out), .in3(multiplexer_72_out),
    .out(multiplexer_104_out), .sel(selector_4));
  Multiplexer #(.select(2)) multiplexer_105 (
    .in0(multiplexer_73_out), .in1(multiplexer_65_out), .in2(multiplexer_81_out), .in3(multiplexer_73_out),
    .out(multiplexer_105_out), .sel(selector_4));
  Multiplexer #(.select(2)) multiplexer_106 (
    .in0(multiplexer_74_out), .in1(multiplexer_66_out), .in2(multiplexer_82_out), .in3(multiplexer_74_out),
    .out(multiplexer_106_out), .sel(selector_4));
  Multiplexer #(.select(2)) multiplexer_107 (
    .in0(multiplexer_75_out), .in1(multiplexer_67_out), .in2(multiplexer_83_out), .in3(multiplexer_75_out),
    .out(multiplexer_107_out), .sel(selector_4));
  Multiplexer #(.select(2)) multiplexer_108 (
    .in0(multiplexer_76_out), .in1(multiplexer_68_out), .in2(multiplexer_84_out), .in3(multiplexer_76_out),
    .out(multiplexer_108_out), .sel(selector_4));
  Multiplexer #(.select(2)) multiplexer_109 (
    .in0(multiplexer_77_out), .in1(multiplexer_69_out), .in2(multiplexer_85_out), .in3(multiplexer_77_out),
    .out(multiplexer_109_out), .sel(selector_4));
  Multiplexer #(.select(2)) multiplexer_110 (
    .in0(multiplexer_78_out), .in1(multiplexer_70_out), .in2(multiplexer_86_out), .in3(multiplexer_78_out),
    .out(multiplexer_110_out), .sel(selector_4));
  Multiplexer #(.select(2)) multiplexer_111 (
    .in0(multiplexer_79_out), .in1(multiplexer_71_out), .in2(multiplexer_87_out), .in3(multiplexer_79_out),
    .out(multiplexer_111_out), .sel(selector_4));
  Multiplexer #(.select(2)) multiplexer_112 (
    .in0(multiplexer_80_out), .in1(multiplexer_72_out), .in2(multiplexer_88_out), .in3(multiplexer_80_out),
    .out(multiplexer_112_out), .sel(selector_4));
  Multiplexer #(.select(2)) multiplexer_113 (
    .in0(multiplexer_81_out), .in1(multiplexer_73_out), .in2(multiplexer_89_out), .in3(multiplexer_81_out),
    .out(multiplexer_113_out), .sel(selector_4));
  Multiplexer #(.select(2)) multiplexer_114 (
    .in0(multiplexer_82_out), .in1(multiplexer_74_out), .in2(multiplexer_90_out), .in3(multiplexer_82_out),
    .out(multiplexer_114_out), .sel(selector_4));
  Multiplexer #(.select(2)) multiplexer_115 (
    .in0(multiplexer_83_out), .in1(multiplexer_75_out), .in2(multiplexer_91_out), .in3(multiplexer_83_out),
    .out(multiplexer_115_out), .sel(selector_4));
  Multiplexer #(.select(2)) multiplexer_116 (
    .in0(multiplexer_84_out), .in1(multiplexer_76_out), .in2(multiplexer_92_out), .in3(multiplexer_84_out),
    .out(multiplexer_116_out), .sel(selector_4));
  Multiplexer #(.select(2)) multiplexer_117 (
    .in0(multiplexer_85_out), .in1(multiplexer_77_out), .in2(multiplexer_93_out), .in3(multiplexer_85_out),
    .out(multiplexer_117_out), .sel(selector_4));
  Multiplexer #(.select(2)) multiplexer_118 (
    .in0(multiplexer_86_out), .in1(multiplexer_78_out), .in2(multiplexer_94_out), .in3(multiplexer_86_out),
    .out(multiplexer_118_out), .sel(selector_4));
  Multiplexer #(.select(2)) multiplexer_119 (
    .in0(multiplexer_87_out), .in1(multiplexer_79_out), .in2(multiplexer_95_out), .in3(multiplexer_87_out),
    .out(multiplexer_119_out), .sel(selector_4));
  Multiplexer #(.select(2)) multiplexer_120 (
    .in0(multiplexer_88_out), .in1(multiplexer_80_out), .in2(multiplexer_96_out), .in3(multiplexer_88_out),
    .out(multiplexer_120_out), .sel(selector_4));
  Multiplexer #(.select(2)) multiplexer_121 (
    .in0(multiplexer_89_out), .in1(multiplexer_81_out), .in2(1'b0), .in3(multiplexer_89_out),
    .out(multiplexer_121_out), .sel(selector_4));
  Multiplexer #(.select(2)) multiplexer_122 (
    .in0(multiplexer_90_out), .in1(multiplexer_82_out), .in2(1'b0), .in3(multiplexer_90_out),
    .out(multiplexer_122_out), .sel(selector_4));
  Multiplexer #(.select(2)) multiplexer_123 (
    .in0(multiplexer_91_out), .in1(multiplexer_83_out), .in2(1'b0), .in3(multiplexer_91_out),
    .out(multiplexer_123_out), .sel(selector_4));
  Multiplexer #(.select(2)) multiplexer_124 (
    .in0(multiplexer_92_out), .in1(multiplexer_84_out), .in2(1'b0), .in3(multiplexer_92_out),
    .out(multiplexer_124_out), .sel(selector_4));
  Multiplexer #(.select(2)) multiplexer_125 (
    .in0(multiplexer_93_out), .in1(multiplexer_85_out), .in2(1'b0), .in3(multiplexer_93_out),
    .out(multiplexer_125_out), .sel(selector_4));
  Multiplexer #(.select(2)) multiplexer_126 (
    .in0(multiplexer_94_out), .in1(multiplexer_86_out), .in2(1'b0), .in3(multiplexer_94_out),
    .out(multiplexer_126_out), .sel(selector_4));
  Multiplexer #(.select(2)) multiplexer_127 (
    .in0(multiplexer_95_out), .in1(multiplexer_87_out), .in2(1'b0), .in3(multiplexer_95_out),
    .out(multiplexer_127_out), .sel(selector_4));
  Multiplexer #(.select(2)) multiplexer_128 (
    .in0(multiplexer_96_out), .in1(multiplexer_88_out), .in2(1'b0), .in3(multiplexer_96_out),
    .out(multiplexer_128_out), .sel(selector_4));
  Multiplexer #(.select(2)) multiplexer_129 (
    .in0(multiplexer_97_out), .in1(1'b0), .in2(multiplexer_113_out), .in3(multiplexer_97_out), .out(C[0]),
    .sel(selector_5));
  Multiplexer #(.select(2)) multiplexer_130 (
    .in0(multiplexer_98_out), .in1(1'b0), .in2(multiplexer_114_out), .in3(multiplexer_98_out), .out(C[1]),
    .sel(selector_5));
  Multiplexer #(.select(2)) multiplexer_131 (
    .in0(multiplexer_99_out), .in1(1'b0), .in2(multiplexer_115_out), .in3(multiplexer_99_out), .out(C[2]),
    .sel(selector_5));
  Multiplexer #(.select(2)) multiplexer_132 (
    .in0(multiplexer_100_out), .in1(1'b0), .in2(multiplexer_116_out), .in3(multiplexer_100_out), .out(C[3]),
    .sel(selector_5));
  Multiplexer #(.select(2)) multiplexer_133 (
    .in0(multiplexer_101_out), .in1(1'b0), .in2(multiplexer_117_out), .in3(multiplexer_101_out), .out(C[4]),
    .sel(selector_5));
  Multiplexer #(.select(2)) multiplexer_134 (
    .in0(multiplexer_102_out), .in1(1'b0), .in2(multiplexer_118_out), .in3(multiplexer_102_out), .out(C[5]),
    .sel(selector_5));
  Multiplexer #(.select(2)) multiplexer_135 (
    .in0(multiplexer_103_out), .in1(1'b0), .in2(multiplexer_119_out), .in3(multiplexer_103_out), .out(C[6]),
    .sel(selector_5));
  Multiplexer #(.select(2)) multiplexer_136 (
    .in0(multiplexer_104_out), .in1(1'b0), .in2(multiplexer_120_out), .in3(multiplexer_104_out), .out(C[7]),
    .sel(selector_5));
  Multiplexer #(.select(2)) multiplexer_137 (
    .in0(multiplexer_105_out), .in1(1'b0), .in2(multiplexer_121_out), .in3(multiplexer_105_out), .out(C[8]),
    .sel(selector_5));
  Multiplexer #(.select(2)) multiplexer_138 (
    .in0(multiplexer_106_out), .in1(1'b0), .in2(multiplexer_122_out), .in3(multiplexer_106_out), .out(C[9]),
    .sel(selector_5));
  Multiplexer #(.select(2)) multiplexer_139 (
    .in0(multiplexer_107_out), .in1(1'b0), .in2(multiplexer_123_out), .in3(multiplexer_107_out), .out(C[10]),
    .sel(selector_5));
  Multiplexer #(.select(2)) multiplexer_140 (
    .in0(multiplexer_108_out), .in1(1'b0), .in2(multiplexer_124_out), .in3(multiplexer_108_out), .out(C[11]),
    .sel(selector_5));
  Multiplexer #(.select(2)) multiplexer_141 (
    .in0(multiplexer_109_out), .in1(1'b0), .in2(multiplexer_125_out), .in3(multiplexer_109_out), .out(C[12]),
    .sel(selector_5));
  Multiplexer #(.select(2)) multiplexer_142 (
    .in0(multiplexer_110_out), .in1(1'b0), .in2(multiplexer_126_out), .in3(multiplexer_110_out), .out(C[13]),
    .sel(selector_5));
  Multiplexer #(.select(2)) multiplexer_143 (
    .in0(multiplexer_111_out), .in1(1'b0), .in2(multiplexer_127_out), .in3(multiplexer_111_out), .out(C[14]),
    .sel(selector_5));
  Multiplexer #(.select(2)) multiplexer_144 (
    .in0(multiplexer_112_out), .in1(1'b0), .in2(multiplexer_128_out), .in3(multiplexer_112_out), .out(C[15]),
    .sel(selector_5));
  Multiplexer #(.select(2)) multiplexer_145 (
    .in0(multiplexer_113_out), .in1(multiplexer_97_out), .in2(1'b0), .in3(multiplexer_113_out), .out(C[16]),
    .sel(selector_5));
  Multiplexer #(.select(2)) multiplexer_146 (
    .in0(multiplexer_114_out), .in1(multiplexer_98_out), .in2(1'b0), .in3(multiplexer_114_out), .out(C[17]),
    .sel(selector_5));
  Multiplexer #(.select(2)) multiplexer_147 (
    .in0(multiplexer_115_out), .in1(multiplexer_99_out), .in2(1'b0), .in3(multiplexer_115_out), .out(C[18]),
    .sel(selector_5));
  Multiplexer #(.select(2)) multiplexer_148 (
    .in0(multiplexer_116_out), .in1(multiplexer_100_out), .in2(1'b0), .in3(multiplexer_116_out), .out(C[19]),
    .sel(selector_5));
  Multiplexer #(.select(2)) multiplexer_149 (
    .in0(multiplexer_117_out), .in1(multiplexer_101_out), .in2(1'b0), .in3(multiplexer_117_out), .out(C[20]),
    .sel(selector_5));
  Multiplexer #(.select(2)) multiplexer_150 (
    .in0(multiplexer_118_out), .in1(multiplexer_102_out), .in2(1'b0), .in3(multiplexer_118_out), .out(C[21]),
    .sel(selector_5));
  Multiplexer #(.select(2)) multiplexer_151 (
    .in0(multiplexer_119_out), .in1(multiplexer_103_out), .in2(1'b0), .in3(multiplexer_119_out), .out(C[22]),
    .sel(selector_5));
  Multiplexer #(.select(2)) multiplexer_152 (
    .in0(multiplexer_120_out), .in1(multiplexer_104_out), .in2(1'b0), .in3(multiplexer_120_out), .out(C[23]),
    .sel(selector_5));
  Multiplexer #(.select(2)) multiplexer_153 (
    .in0(multiplexer_121_out), .in1(multiplexer_105_out), .in2(1'b0), .in3(multiplexer_121_out), .out(C[24]),
    .sel(selector_5));
  Multiplexer #(.select(2)) multiplexer_154 (
    .in0(multiplexer_122_out), .in1(multiplexer_106_out), .in2(1'b0), .in3(multiplexer_122_out), .out(C[25]),
    .sel(selector_5));
  Multiplexer #(.select(2)) multiplexer_155 (
    .in0(multiplexer_123_out), .in1(multiplexer_107_out), .in2(1'b0), .in3(multiplexer_123_out), .out(C[26]),
    .sel(selector_5));
  Multiplexer #(.select(2)) multiplexer_156 (
    .in0(multiplexer_124_out), .in1(multiplexer_108_out), .in2(1'b0), .in3(multiplexer_124_out), .out(C[27]),
    .sel(selector_5));
  Multiplexer #(.select(2)) multiplexer_157 (
    .in0(multiplexer_125_out), .in1(multiplexer_109_out), .in2(1'b0), .in3(multiplexer_125_out), .out(C[28]),
    .sel(selector_5));
  Multiplexer #(.select(2)) multiplexer_158 (
    .in0(multiplexer_126_out), .in1(multiplexer_110_out), .in2(1'b0), .in3(multiplexer_126_out), .out(C[29]),
    .sel(selector_5));
  Multiplexer #(.select(2)) multiplexer_159 (
    .in0(multiplexer_127_out), .in1(multiplexer_111_out), .in2(1'b0), .in3(multiplexer_127_out), .out(C[30]),
    .sel(selector_5));
  Multiplexer #(.select(2)) multiplexer_160 (
    .in0(multiplexer_128_out), .in1(multiplexer_112_out), .in2(1'b0), .in3(multiplexer_128_out), .out(C[31]),
    .sel(selector_5));
endmodule

module ALU (
  input  [31:0] A,
  input  [31:0] B,
  input  [2:0] sel,
  output zero,
  output [31:0] C
);

  wire not_1_out;
  wire [31:0] add_sub_1_c, and_1_out, bit_shifter_test_1_c, not_2_out, or_1_out, xor_1_out;

  not not_1 (not_1_out, sel[0]);
  add_sub add_sub_1 (.A(A), .B(B), .sub(sel[0]), .C(add_sub_1_c));
  assign and_1_out = A & B;  // AND_Gate and_1, 32 bits wide
  assign or_1_out = A | B;  // OR_Gate or_1, 32 bits wide
  assign xor_1_out = A ^ B;  // XOR_Gate xor_1, 32 bits wide
  assign not_2_out = ~A;  // NOT_Gate not_2, 32 bits wide
  bit_shifter_test bit_shifter_test_1 (.A(A), .L(sel[0]), .R(not_1_out), .B(B[4:0]), .C(bit_shifter_test_1_c));
  Multiplexer #(.select(3), .width(32)) multiplexer_1 (
    .in0(add_sub_1_c), .in1(add_sub_1_c), .in2(and_1_out), .in3(or_1_out), .in4(xor_1_out), .in5(not_2_out),
    .in6(bit_shifter_test_1_c), .in7(bit_shifter_test_1_c), .out(C), .sel(sel));
  nor nor_1 (zero, C[0], C[1], C[2], C[3], C[4], C[5], C[6], C[7], C[8], C[9], C[10], C[11], C[12], C[13], C[14], C[15], C[16], C[17], C[18], C[19], C[20], C[21], C[22], C[23], C[24], C[25], C[26], C[27], C[28], C[29], C[30], C[31]);
endmodule

module IM (
  input  [23:0] in_1,
  output [31:0] out_2
);

  ROM #(.addrWidth(24), .dataWidth(32)) rom_1 (.addr(in_1), .data(out_2));

  // Notes on the sheet:
  //   contents of rom_1 (hex, n*v repeats v):
  //   0 b10100db b20200c7 11230002 c3000002 21240002 c4000002 31250002 c5000002 41260002 c6000002 51270002
  //   c7000002 61080002 c8000002 71490002 c9000002 824a0002 ca000002 910b0002 cb000002 a10c0002 cc000002
  //   b10d0002 cd000002 d0000002 112e0002 e1100002 112e0002 f0000002
endmodule

module MC (
  input  [3:0] in_1,
  output display,
  output WE_RB,
  output salto,
  output desvio,
  output fim,
  output sel_b_const,
  output [2:0] sel_ula
);

  ROM #(.addrWidth(4), .dataWidth(9)) rom_1 (
    .addr(in_1), .data({sel_ula, sel_b_const, fim, desvio, salto, WE_RB, display}));

  // Notes on the sheet:
  //   contents of rom_1 (hex, n*v repeats v):
  //   0 2 42 82 c2 102 142 182 1c2 e2 122 22 1 4 48 10
endmodule

module IP (
  input  [31:0] instruction,
  input  fim,
  input  clock,
  input  reset,
  output [31:0] out_5
);

  wire not_1_out;

  Register #(.width(32)) register_1 (.D(instruction), .en(not_1_out), .clk(clock), .Q(out_5), .clr(reset));
  not not_1 (not_1_out, fim);
endmodule

module display (
  input  [31:0] A,
  input  WE,
  input  clock,
  input  reset,
  output [31:0] display_A
);

  Register #(.width(32)) register_1 (.D(A), .en(WE), .clk(clock), .Q(display_A), .clr(reset));
endmodule
